// Logisim project item_a.circ as structural Verilog: 1 circuit, main circuit item_a
module item_a (
  input  A,
  input  B,
  input  C,
  output x
);

  wire and_1_out, nand_1_out, not_1_out, not_2_out;

  not not_1 (not_1_out, A);
  not not_2 (not_2_out, B);
  nand nand_1 (nand_1_out, not_1_out, not_2_out);
  and and_1 (and_1_out, B, C);
  or or_1 (x, nand_1_out, and_1_out);
endmodule
