// Logisim project item_b.circ as structural Verilog: 1 circuit, main circuit item_b
module item_b (
  input  A,
  input  B,
  input  C,
  input  D,
  output x
);

  wire and_1_out, and_2_out, and_3_out, not_1_out, not_2_out, not_3_out, not_4_out, not_5_out, not_6_out,
       not_7_out;

  not not_1 (not_1_out, A);
  not not_2 (not_2_out, B);
  and and_1 (and_1_out, not_1_out, not_2_out, not_3_out);
  not not_3 (not_3_out, C);
  not not_4 (not_4_out, B);
  and and_2 (and_2_out, A, not_4_out, not_5_out);
  not not_5 (not_5_out, C);
  not not_6 (not_6_out, A);
  and and_3 (and_3_out, not_6_out, not_7_out, D);
  not not_7 (not_7_out, B);
  or or_1 (x, and_1_out, and_2_out, and_3_out);
endmodule
