// Logisim project questao05.circ as structural Verilog: 1 circuit, main circuit questao05
module questao05 (
  input  B2,
  input  B1,
  input  B0,
  output y0,
  output y1,
  output y2
);

  wire and_2_out, and_3_out, and_4_out, not_1_out, not_2_out, not_3_out, not_4_out;

  not not_1 (not_1_out, B0);
  not not_2 (not_2_out, B1);
  not not_3 (not_3_out, B2);
  not not_4 (not_4_out, B1);
  and and_1 (y2, B2, B1);
  and and_2 (and_2_out, B0, B1);
  and and_3 (and_3_out, B0, B2);
  and and_4 (and_4_out, not_1_out, not_2_out, not_3_out);
  and and_5 (y1, B2, not_4_out);
  or or_1 (y0, and_2_out, and_3_out, and_4_out);
endmodule
