// Logisim project Somador16Bits.circ as structural Verilog: 4 circuits, main circuit Half-Adder
module Half_Adder (
  input  A,
  input  B,
  output S,
  output C
);

  xor xor_1 (S, A, B);
  and and_1 (C, A, B);
endmodule

module Full_Adder (
  input  C_in,
  input  A,
  input  B,
  output S,
  output C_out
);

  wire half_adder_1_c, half_adder_1_s, half_adder_2_c;

  Half_Adder half_adder_1 (.A(A), .B(B), .S(half_adder_1_s), .C(half_adder_1_c));
  Half_Adder half_adder_2 (.A(C_in), .B(half_adder_1_s), .S(S), .C(half_adder_2_c));
  or or_1 (C_out, half_adder_2_c, half_adder_1_c);
endmodule

module Somador_8_Bits (
  input  C0,
  input  A0,
  input  B0,
  input  A1,
  input  B1,
  input  A2,
  input  B2,
  input  A3,
  input  B3,
  output S0,
  output S1,
  output S2,
  output S3,
  output C_out
);

  wire full_adder_1_c_out, full_adder_2_c_out, full_adder_3_c_out;

  Full_Adder full_adder_1 (.C_in(C0), .A(A0), .B(B0), .S(S0), .C_out(full_adder_1_c_out));
  Full_Adder full_adder_2 (.C_in(full_adder_1_c_out), .A(A1), .B(B1), .S(S1), .C_out(full_adder_2_c_out));
  Full_Adder full_adder_3 (.C_in(full_adder_2_c_out), .A(A2), .B(B2), .S(S2), .C_out(full_adder_3_c_out));
  Full_Adder full_adder_4 (.C_in(full_adder_3_c_out), .A(A3), .B(B3), .S(S3), .C_out(C_out));
endmodule

module Somador_16bits (
  input  CO,
  input  A0,
  input  B0,
  input  A1,
  input  B1,
  input  A2,
  input  B2,
  input  A4,
  input  B4,
  input  A3,
  input  B3,
  input  A5,
  input  B5,
  input  A6,
  input  B6,
  input  A7,
  input  B7,
  output S0,
  output S1,
  output S2,
  output S3,
  output S4,
  output S5,
  output S6,
  output S7
);

  wire somador_8_bits_1_c_out;

  Somador_8_Bits somador_8_bits_1 (
    .C0(CO), .A0(A0), .B0(B0), .A1(A1), .B1(B1), .A2(A2), .B2(B2), .A3(A3), .B3(B3), .S0(S0), .S1(S1),
    .S2(S2), .S3(S3), .C_out(somador_8_bits_1_c_out));
  Somador_8_Bits somador_8_bits_2 (
    .C0(somador_8_bits_1_c_out), .A0(A4), .B0(B4), .A1(A5), .B1(B5), .A2(A6), .B2(B6), .A3(A7), .B3(B7),
    .S0(S4), .S1(S5), .S2(S6), .S3(S7));  // open: C_out
endmodule
